# Fritzing sketch 06-motor-driver (saved by Fritzing 1.0.4)
breadboards: 1

parts:
  M4 = DC Motor [voltage_(max)=6V voltage_(min)=3V]
  M5 = DC Motor [voltage_(max)=6V voltage_(min)=3V]
  Part2 = SparkFun Motor Driver TB6612FNG (v11) [part_number=ROB-14451]
  A1 = ESP32 38Pin narrow
  BAT1 = BC9VPC [package=bc9vpc]
  A2 = mini560 [package=THT]

nets:
  N1: M4.pin_1, Part2.B01
  N2: M4.pin_2, Part2.B02
  N3: M5.pin_1, Part2.A01
  N4: M5.pin_2, Part2.A02
  N5: Part2.GND, A1.Pin_14, A1.Pin_32, A1.Pin_38, BAT1.V-, A2.pin_4, A2.pin_7
  N6: Part2.VCC, A1.Pin_1
  N7: Part2.VM, A2.pin_8, A2.pin_9
  N8: Part2.PWMA, A1.Pin_37
  N9: Part2.AIN2, A1.Pin_31
  N10: Part2.AIN1, A1.Pin_30
  N11: Part2.STBY, A1.Pin_8
  N12: Part2.BIN1, A1.Pin_10
  N13: Part2.BIN2, A1.Pin_11
  N14: Part2.PWMB, A1.Pin_29
  N15: BAT1.V+, A2.pin_1

custom parts:
  SparkFun Motor Driver TB6612FNG (v11): The TB6612FNG Motor Driver can control up to two DC motors at a constant current of 1.2A (3.2A peak). Two input signals (IN1 and IN2) can be used to control the motor in one of four function modes: CW, CCW, short-brake and stop. The two motor outputs (A and B) can be separately controlled, and the speed of each motor is controlled via a PWM input signal with a frequency up to 100kHz. The STBY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
  ESP32 38Pin narrow: ESP32 38Pin narrow.
  mini560: 5A DC-DC Mini 560 Step Down Stabilized Voltage Supply Module Output 3.3 5V 9V 12V Step-down Power Converter Board Module
