# Fritzing sketch 07-ky-023 (saved by Fritzing 1.0.4)

parts:
  A1 = ESP32 38Pin narrow
  Part1 = Thumb Joystick

nets:
  N1: A1.Pin_1, Part1.VCC
  N2: A1.Pin_5, Part1.HORZ
  N3: A1.Pin_6, Part1.VERT
  N4: A1.Pin_7, Part1.SEL
  N5: A1.Pin_38, Part1.GND

custom parts:
  ESP32 38Pin narrow: ESP32 38Pin narrow.
