# Fritzing sketch main-schema (saved by Fritzing 1.0.4)

parts:
  A1 = ESP32 38Pin narrow
  A3 = BMI160 breakout
  SERVO2 = Tower Pro SG90 servo [part_number=101246]
  BAT2 = BC9VPC [package=bc9vpc]
  A4 = mini560 [package=THT]
  Part1 = SparkFun Motor Driver TB6612FNG (v11) [part_number=ROB-14451]
  M6 = DC Motor [voltage_(max)=6V voltage_(min)=3V]
  M7 = DC Motor [voltage_(max)=6V voltage_(min)=3V]

nets:
  +5V: A1.Pin_1, A3.Pin_7, SERVO2.+5V, Part1.VCC
  N1: A1.Pin_8, Part1.STBY
  N2: A1.Pin_10, Part1.BIN1
  N3: A1.Pin_11, Part1.BIN2
  GND: A1.Pin_14, A1.Pin_38, A3.Pin_8, SERVO2.GND, BAT2.V-, A4.pin_3, A4.pin_6, A4.pin_7, Part1.GND
  N4: A1.Pin_23, SERVO2.Signal
  N5: A1.Pin_26, A3.Pin_9
  N6: A1.Pin_27, A3.Pin_10
  N7: A1.Pin_28, A3.Pin_11
  N8: A1.Pin_29, Part1.PWMB
  N9: A1.Pin_30, Part1.AIN1
  N10: A1.Pin_31, Part1.AIN2
  N11: A1.Pin_33, A3.Pin_12
  N12: A1.Pin_37, Part1.PWMA
  N13: BAT2.V+, A4.pin_1, A4.pin_2
  N14: A4.pin_9, Part1.VM
  N15: Part1.B01, M7.pin_1
  N16: Part1.B02, M7.pin_2
  N17: Part1.A02, M6.pin_2
  N18: Part1.A01, M6.pin_1

custom parts:
  ESP32 38Pin narrow: ESP32 38Pin narrow.
  BMI160 breakout: BMI160 Latest Stance Accelerometer Gyroscope module 6 Dof inertial Measurement Sensors.
  Tower Pro SG90 servo: Original file by John De Cristofaro http://www.adafruit.com/products/1449 Adafruit Feedback Servo (Small) Edited by: e-radionica.com 28/9/2015
  mini560: 5A DC-DC Mini 560 Step Down Stabilized Voltage Supply Module Output 3.3 5V 9V 12V Step-down Power Converter Board Module
  SparkFun Motor Driver TB6612FNG (v11): The TB6612FNG Motor Driver can control up to two DC motors at a constant current of 1.2A (3.2A peak). Two input signals (IN1 and IN2) can be used to control the motor in one of four function modes: CW, CCW, short-brake and stop. The two motor outputs (A and B) can be separately controlled, and the speed of each motor is controlled via a PWM input signal with a frequency up to 100kHz. The STBY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
