# Fritzing sketch 04-bmi16-schema (saved by Fritzing 1.0.4)

parts:
  A1 = ESP32 38Pin narrow
  A2 = BMI160 breakout

nets:
  N1: A1.Pin_1, A2.Pin_7
  N2: A1.Pin_30, A2.Pin_9
  N3: A1.Pin_31, A2.Pin_12
  N4: A1.Pin_32, A1.Pin_38, A2.Pin_8
  N5: A1.Pin_33, A2.Pin_11
  N6: A1.Pin_37, A2.Pin_10

custom parts:
  ESP32 38Pin narrow: ESP32 38Pin narrow.
  BMI160 breakout: BMI160 Latest Stance Accelerometer Gyroscope module 6 Dof inertial Measurement Sensors.
