# Fritzing sketch 05-servo-schema (saved by Fritzing 1.0.4)

parts:
  A1 = ESP32 38Pin narrow
  SERVO1 = Tower Pro SG90 servo [part_number=101246]

nets:
  N1: A1.Pin_1, SERVO1.+5V
  N2: A1.Pin_23, SERVO1.Signal
  N3: A1.Pin_38, SERVO1.GND

custom parts:
  ESP32 38Pin narrow: ESP32 38Pin narrow.
  Tower Pro SG90 servo: Original file by John De Cristofaro http://www.adafruit.com/products/1449 Adafruit Feedback Servo (Small) Edited by: e-radionica.com 28/9/2015
